# Fritzing sketch BH1750 (saved by Fritzing 1.0.6)
breadboards: 1

parts:
  esp1 = ESP32 DevKitc V4
  Part1 = BH1750

nets:
  3V3: esp1.3V3, Part1.VCC
  N1: esp1.IO32, Part1.SDA
  N2: esp1.IO33, Part1.SCL
  GND: esp1.GND, Part1.GND

notes:
  GPIO32
  GPIO33

custom parts:
  ESP32 DevKitc V4: ESP32-DevKitC board with ESP32-WROOM-32 module. ESP32-DevKitC V4 is a small-sized ESP32-based development board produced by Espressif. Most of the pins on the ESP module are broken out to the pin headers on the board. The pins D0, D1, D2, D3, CMD and CLK are used internally for communication between ESP32 and SPI flash memory. They are grouped on both sides near the USB connector. Avoid using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
  BH1750: Light Sensor
