# Fritzing sketch Relay_2 (saved by Fritzing 1.0.6)
breadboards: 1

parts:
  esp1 = ESP32 DevKitc V4
  A1 = 2 channel relay module [package=THT]
  J1 = 2.1mm Barrel Jack with Terminal Block
  DotStar1 = DotStar LED Strip [mn=Adafruit mpn=2239 part_number=2239]
  L1 = Solenoid
  J2 = 2.1mm Barrel Jack with Terminal Block

nets:
  N1: esp1.IO25, A1.pin_15
  N2: esp1.IO26, A1.pin_16
  N3: esp1.GND, A1.pin_14
  N4: esp1.5V, A1.pin_13
  N5: A1.pin_1, J2.POS
  N6: A1.pin_2, L1.pin2
  N7: A1.pin_4, J1.POS
  N8: A1.pin_5, DotStar1.+5V
  N9: J1.NEG, DotStar1.GND

notes:
  GPIO25
  GPIO26
  Solenoid 12v
  LED 5v
  5v Adapter
  12v Adapter

custom parts:
  ESP32 DevKitc V4: ESP32-DevKitC board with ESP32-WROOM-32 module. ESP32-DevKitC V4 is a small-sized ESP32-based development board produced by Espressif. Most of the pins on the ESP module are broken out to the pin headers on the board. The pins D0, D1, D2, D3, CMD and CLK are used internally for communication between ESP32 and SPI flash memory. They are grouped on both sides near the USB connector. Avoid using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
  2 channel relay module: 2 channel Relay Module 5V 12V 24V High and Low Level Trigger Relay Control With Optocoupler Two Way relays DC 5 V 12 V 24 V Volt.
