# Fritzing sketch TDS_with_probe (saved by Fritzing 1.0.6)
breadboards: 1

parts:
  esp1 = ESP32 DevKitc V4
  A1 = tds-sensor-meter-v1.0_1

nets:
  N1: esp1.3V3, A1.pin2
  N2: esp1.VN, A1.pin1
  N3: esp1.GND, A1.pin3

notes:
  GPIO39

custom parts:
  ESP32 DevKitc V4: ESP32-DevKitC board with ESP32-WROOM-32 module. ESP32-DevKitC V4 is a small-sized ESP32-based development board produced by Espressif. Most of the pins on the ESP module are broken out to the pin headers on the board. The pins D0, D1, D2, D3, CMD and CLK are used internally for communication between ESP32 and SPI flash memory. They are grouped on both sides near the USB connector. Avoid using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
  : TDS Meter V1.0 Development Board Water Meter Filter Measuring Water Sensor Module.
