# Fritzing sketch Combined (saved by Fritzing 1.0.6)
breadboards: 2

parts:
  esp1 = ESP32 DevKitc V4
  A1 = 2 channel relay module [package=THT]
  A2 = 2 channel relay module [package=THT]
  M2 = seeed grove atomizer v1.0
  WATER_PUMP2 = water pump/motor  # not connected
  A3 = tds-sensor-meter-v1.0_1
  Part2 = BH1750
  Water_Level_Sensor2 = Water Level Sensor
  Capacitive_Soil_Moisture_Sensor2 = DFRobot Capacitive Soil Moisture Sensor V1.0 [part_number=SEN0193]
  R2 = Resistor [tolerance=±5% power=0.25W resistance=220 package=THT]
  LED2 = LED - 5mm [color="Green (555nm)" current=0.030A package="5 mm [THT]"]
  DHT3 = DHT22 Humidity and Temperature Sensor
  LED3 = LED - 5mm [color="Blue (430nm)" current=0.030A package="5 mm [THT]"]
  R3 = Resistor [tolerance=±5% power=0.25W resistance=220 package=THT]
  JACK1 = 2.1mm Barrel Jack with Terminal Block
  JACK2 = 2.1mm Barrel Jack with Terminal Block
  DotStar2 = DotStar LED Strip [mn=Adafruit mpn=2239 part_number=2239]
  F2 = Fan - Ventilador [package=THT]

nets:
  N1: esp1.IO2, R2.Pin_0
  N2: esp1.IO0, R3.Pin_0
  N3: esp1.IO4, DHT3.DATA
  N4: esp1.GND#18, LED2.cathode, DHT3.GND, LED3.cathode
  3V3: esp1.3V3, DHT3.VDD
  N5: esp1.VN, A3.pin1
  N6: esp1.IO34, Water_Level_Sensor2.SIG
  N7: esp1.IO35, Capacitive_Soil_Moisture_Sensor2.A
  N8: esp1.IO32, Part2.SDA
  N9: esp1.IO33, Part2.SCL
  N10: esp1.IO26, A1.pin_16
  N11: esp1.IO14, A2.pin_16
  N12: esp1.IO12, A2.pin_15
  GND: esp1.GND#32, A1.pin_14, A2.pin_14, A3.pin3, Part2.GND, Water_Level_Sensor2.GND, Capacitive_Soil_Moisture_Sensor2.GND
  VCC: esp1.5V, A1.pin_13, A2.pin_13, A3.pin2, Part2.VCC, Water_Level_Sensor2.VCC, Capacitive_Soil_Moisture_Sensor2.VCC
  N13: A1.pin_1, A1.pin_4, JACK1.POS
  N14: A1.pin_2, DotStar2.+5V
  N15: A1.pin_5, F2.5V
  N16: A2.pin_1, A2.pin_4, JACK2.POS
  N17: A2.pin_2, M2.VCC
  N18: M2.GND, JACK2.NEG
  N19: R2.Pin_1, LED2.anode
  N20: LED3.anode, R3.Pin_1
  GND_2: JACK1.NEG, DotStar2.GND, F2.GND

notes:
  GPIO26
  5v Adapter
  Mist Maker 5v
  Submersible Water Pump 5v
  GPIO14
  GPIO12
  GPIO4
  GPIO2
  GPIO0
  GPIO39
  GPIO35
  GPIO34
  GPIO33
  GPIO32
  5V Fan
  LED Stripe White
  GPIO25

custom parts:
  ESP32 DevKitc V4: ESP32-DevKitC board with ESP32-WROOM-32 module. ESP32-DevKitC V4 is a small-sized ESP32-based development board produced by Espressif. Most of the pins on the ESP module are broken out to the pin headers on the board. The pins D0, D1, D2, D3, CMD and CLK are used internally for communication between ESP32 and SPI flash memory. They are grouped on both sides near the USB connector. Avoid using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
  2 channel relay module: 2 channel Relay Module 5V 12V 24V High and Low Level Trigger Relay Control With Optocoupler Two Way relays DC 5 V 12 V 24 V Volt.
  seeed grove atomizer v1.0: Grove - Water Atomization is a perfect module for you to quickly DIY a humidifier with Arduino. You can also develop more advanced and interesting projects with digital scent technology and any other situations in which atomization required.
  water pump/motor: WATER PUMP BY ARDUBLOCKTR
  : TDS Meter V1.0 Development Board Water Meter Filter Measuring Water Sensor Module.
  BH1750: Light Sensor
  Water Level Sensor: A water level sensor. This sensor operates at 3V to 5V. The Sig (signal) pin outputs an analogue signal that is in proportion to the amount of water in contact with the sensor.
  DFRobot Capacitive Soil Moisture Sensor V1.0: DFRobot Capacitive Soil Moisture Sensor V1.0 This product measures soil moisture levels by capacitive sensing, rather than resistive sensing like other types of moisture sensor. It is made of a corrosion resistant material giving it a long service life. Insert it into soil and impress your friends with the real-time soil moisture data! The product includes an on-board voltage regulator which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
  Fan - Ventilador: Ventilador de 2 pines, se encuentra comunmente en computadoras de escritorio
