# Fritzing sketch Relay_1 (saved by Fritzing 1.0.6)
breadboards: 1

parts:
  esp1 = ESP32 DevKitc V4
  A1 = 2 channel relay module [package=THT]
  M1 = seeed grove atomizer v1.0
  JACK1 = 2.1mm Barrel Jack with Terminal Block
  WATER_PUMP1 = water pump/motor  # not connected

nets:
  N1: esp1.IO14, A1.pin_16
  N2: esp1.IO12, A1.pin_15
  N3: esp1.GND, A1.pin_14
  N4: esp1.5V, A1.pin_13
  N5: A1.pin_1, A1.pin_4, JACK1.POS
  N6: A1.pin_2, M1.VCC
  N7: M1.GND, JACK1.NEG

notes:
  GPIO12
  GPIO14
  Submersible Water Pump 5v
  Mist Maker 5v

custom parts:
  ESP32 DevKitc V4: ESP32-DevKitC board with ESP32-WROOM-32 module. ESP32-DevKitC V4 is a small-sized ESP32-based development board produced by Espressif. Most of the pins on the ESP module are broken out to the pin headers on the board. The pins D0, D1, D2, D3, CMD and CLK are used internally for communication between ESP32 and SPI flash memory. They are grouped on both sides near the USB connector. Avoid using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
  2 channel relay module: 2 channel Relay Module 5V 12V 24V High and Low Level Trigger Relay Control With Optocoupler Two Way relays DC 5 V 12 V 24 V Volt.
  seeed grove atomizer v1.0: Grove - Water Atomization is a perfect module for you to quickly DIY a humidifier with Arduino. You can also develop more advanced and interesting projects with digital scent technology and any other situations in which atomization required.
  water pump/motor: WATER PUMP BY ARDUBLOCKTR
