# Fritzing sketch Relay_2 (saved by Fritzing 1.0.6)
breadboards: 1

parts:
  esp1 = ESP32 DevKitc V4
  A1 = 2 channel relay module [package=THT]
  JACK1 = 2.1mm Barrel Jack with Terminal Block
  DotStar1 = DotStar LED Strip [mn=Adafruit mpn=2239 part_number=2239]
  F1 = Fan - Ventilador [package=THT]

nets:
  N1: esp1.IO25, A1.pin_15
  N2: esp1.IO26, A1.pin_16
  N3: esp1.GND, A1.pin_14
  N4: esp1.5V, A1.pin_13
  N5: A1.pin_1, A1.pin_3, A1.pin_4, JACK1.POS
  N6: A1.pin_2, DotStar1.+5V
  N7: A1.pin_5, F1.5V
  GND: JACK1.NEG, DotStar1.GND, F1.GND

notes:
  GPIO26
  5v Adapter
  GPIO25
  LED Stripe White
  5V Fan

custom parts:
  ESP32 DevKitc V4: ESP32-DevKitC board with ESP32-WROOM-32 module. ESP32-DevKitC V4 is a small-sized ESP32-based development board produced by Espressif. Most of the pins on the ESP module are broken out to the pin headers on the board. The pins D0, D1, D2, D3, CMD and CLK are used internally for communication between ESP32 and SPI flash memory. They are grouped on both sides near the USB connector. Avoid using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
  2 channel relay module: 2 channel Relay Module 5V 12V 24V High and Low Level Trigger Relay Control With Optocoupler Two Way relays DC 5 V 12 V 24 V Volt.
  Fan - Ventilador: Ventilador de 2 pines, se encuentra comunmente en computadoras de escritorio
