# Fritzing sketch Soil (saved by Fritzing 1.0.6)
breadboards: 1

parts:
  esp1 = ESP32 DevKitc V4
  Capacitive_Soil_Moisture_Sensor1 = DFRobot Capacitive Soil Moisture Sensor V1.0 [part_number=SEN0193]

nets:
  3V3: esp1.3V3, Capacitive_Soil_Moisture_Sensor1.VCC
  N1: esp1.IO35, Capacitive_Soil_Moisture_Sensor1.A
  GND: esp1.GND, Capacitive_Soil_Moisture_Sensor1.GND

notes:
  GPIO35

custom parts:
  ESP32 DevKitc V4: ESP32-DevKitC board with ESP32-WROOM-32 module. ESP32-DevKitC V4 is a small-sized ESP32-based development board produced by Espressif. Most of the pins on the ESP module are broken out to the pin headers on the board. The pins D0, D1, D2, D3, CMD and CLK are used internally for communication between ESP32 and SPI flash memory. They are grouped on both sides near the USB connector. Avoid using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
  DFRobot Capacitive Soil Moisture Sensor V1.0: DFRobot Capacitive Soil Moisture Sensor V1.0 This product measures soil moisture levels by capacitive sensing, rather than resistive sensing like other types of moisture sensor. It is made of a corrosion resistant material giving it a long service life. Insert it into soil and impress your friends with the real-time soil moisture data! The product includes an on-board voltage regulator which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
