# Fritzing sketch Water_level (saved by Fritzing 1.0.6)
breadboards: 1

parts:
  esp1 = ESP32 DevKitc V4
  Water_Level_Sensor1 = Water Level Sensor

nets:
  3V3: esp1.3V3, Water_Level_Sensor1.VCC
  N1: esp1.IO34, Water_Level_Sensor1.SIG
  GND: esp1.GND, Water_Level_Sensor1.GND

notes:
  GPIO34

custom parts:
  ESP32 DevKitc V4: ESP32-DevKitC board with ESP32-WROOM-32 module. ESP32-DevKitC V4 is a small-sized ESP32-based development board produced by Espressif. Most of the pins on the ESP module are broken out to the pin headers on the board. The pins D0, D1, D2, D3, CMD and CLK are used internally for communication between ESP32 and SPI flash memory. They are grouped on both sides near the USB connector. Avoid using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
  Water Level Sensor: A water level sensor. This sensor operates at 3V to 5V. The Sig (signal) pin outputs an analogue signal that is in proportion to the amount of water in contact with the sensor.
